// Logisim project FloatingPointAdder.circ as structural Verilog: 25 circuits, main circuit 1 bit right shifter
module _1_bit_right_shifter (
  input  [31:0] in_1,
  output [31:0] out_2
);


  assign out_2 = {1'b0, in_1[31:1]};
endmodule

module _2_bit_right_shifter (
  input  [31:0] in_1,
  output [31:0] out_2
);

  wire [31:0] n1_bit_right_shifter_1_out_2;

  _1_bit_right_shifter u_1_bit_right_shifter_1 (.in_1(in_1), .out_2(n1_bit_right_shifter_1_out_2));
  _1_bit_right_shifter u_1_bit_right_shifter_2 (.in_1(n1_bit_right_shifter_1_out_2), .out_2(out_2));
endmodule

module _4_bit_right_shifter (
  input  [31:0] in_1,
  output [31:0] out_2
);

  wire [31:0] n2_bit_right_shifter_1_out_2;

  _2_bit_right_shifter u_2_bit_right_shifter_1 (.in_1(in_1), .out_2(n2_bit_right_shifter_1_out_2));
  _2_bit_right_shifter u_2_bit_right_shifter_2 (.in_1(n2_bit_right_shifter_1_out_2), .out_2(out_2));
endmodule

module _8_bit_right_shifter (
  input  [31:0] in_1,
  output [31:0] out_2
);

  wire [31:0] n4_bit_right_shifter_1_out_2;

  _4_bit_right_shifter u_4_bit_right_shifter_1 (.in_1(in_1), .out_2(n4_bit_right_shifter_1_out_2));
  _4_bit_right_shifter u_4_bit_right_shifter_2 (.in_1(n4_bit_right_shifter_1_out_2), .out_2(out_2));
endmodule

module _16_bit_right_shifter (
  input  [31:0] in_1,
  output [31:0] out_2
);

  wire [31:0] n8_bit_right_shifter_1_out_2;

  _8_bit_right_shifter u_8_bit_right_shifter_1 (.in_1(in_1), .out_2(n8_bit_right_shifter_1_out_2));
  _8_bit_right_shifter u_8_bit_right_shifter_2 (.in_1(n8_bit_right_shifter_1_out_2), .out_2(out_2));
endmodule

module _1_bit_left_shifter (
  input  [31:0] in_1,
  output [31:0] out_2
);


  assign out_2 = {in_1[30:0], 1'b0};
endmodule

module _2_bit_left_shifter (
  input  [31:0] in_1,
  output [31:0] out_2
);

  wire [31:0] n1_bit_left_shifter_1_out_2;

  _1_bit_left_shifter u_1_bit_left_shifter_1 (.in_1(in_1), .out_2(n1_bit_left_shifter_1_out_2));
  _1_bit_left_shifter u_1_bit_left_shifter_2 (.in_1(n1_bit_left_shifter_1_out_2), .out_2(out_2));
endmodule

module _4_bit_left_shifter (
  input  [31:0] in_1,
  output [31:0] out_2
);

  wire [31:0] n2_bit_left_shifter_1_out_2;

  _2_bit_left_shifter u_2_bit_left_shifter_1 (.in_1(in_1), .out_2(n2_bit_left_shifter_1_out_2));
  _2_bit_left_shifter u_2_bit_left_shifter_2 (.in_1(n2_bit_left_shifter_1_out_2), .out_2(out_2));
endmodule

module _8_bit_left_shifter (
  input  [31:0] in_1,
  output [31:0] out_2
);

  wire [31:0] n4_bit_left_shifter_1_out_2;

  _4_bit_left_shifter u_4_bit_left_shifter_1 (.in_1(in_1), .out_2(n4_bit_left_shifter_1_out_2));
  _4_bit_left_shifter u_4_bit_left_shifter_2 (.in_1(n4_bit_left_shifter_1_out_2), .out_2(out_2));
endmodule

module _16_bit_left_shifter (
  input  [31:0] in_1,
  output [31:0] out_2
);

  wire [31:0] n8_bit_left_shifter_1_out_2;

  _8_bit_left_shifter u_8_bit_left_shifter_1 (.in_1(in_1), .out_2(n8_bit_left_shifter_1_out_2));
  _8_bit_left_shifter u_8_bit_left_shifter_2 (.in_1(n8_bit_left_shifter_1_out_2), .out_2(out_2));
endmodule

module _74157 (
  input  _1__S,
  input  _16__Vcc,
  input  _2__A1,
  input  _15__G,
  input  _3__B1,
  input  _14__A4,
  input  _13__B4,
  input  _5__A2,
  input  _6__B2,
  input  _11__A3,
  input  _10__B3,
  input  _8__GND,
  output _4__Y1,
  output _12__Y4,
  output _7__Y2,
  output _9__Y3
);

  wire multiplexer_1_out, multiplexer_2_out, multiplexer_3_out, multiplexer_4_out, not_1_out;

  Multiplexer #(.enable("false")) multiplexer_1 (.in0(_2__A1), .in1(_3__B1), .out(multiplexer_1_out), .sel(_1__S));
  and and_1 (_4__Y1, multiplexer_1_out, not_1_out);
  Multiplexer #(.enable("false")) multiplexer_2 (.in0(_5__A2), .in1(_6__B2), .out(multiplexer_2_out), .sel(_1__S));
  and and_2 (_7__Y2, multiplexer_2_out, not_1_out);
  not not_1 (not_1_out, _15__G);
  Multiplexer #(.enable("false")) multiplexer_3 (.in0(_14__A4), .in1(_13__B4), .out(multiplexer_3_out), .sel(_1__S));
  and and_3 (_12__Y4, multiplexer_3_out, not_1_out);
  Multiplexer #(.enable("false")) multiplexer_4 (.in0(_11__A3), .in1(_10__B3), .out(multiplexer_4_out), .sel(_1__S));
  and and_4 (_9__Y3, multiplexer_4_out, not_1_out);

  // Notes on the sheet:
  //   74157: Quad 2-Line to 1-Line Multiplexer
endmodule

module _4_bit_num_select (
  input  [3:0] in_1,
  input  [3:0] in_2,
  input  in_3,
  output [3:0] out_4
);

  _74157 u_74157_1 (
    ._1__S(in_3), ._2__A1(in_1[0]), ._3__B1(in_2[0]), ._4__Y1(out_4[0]), ._5__A2(in_1[1]), ._6__B2(in_2[1]),
    ._7__Y2(out_4[1]), ._15__G(1'b0), ._14__A4(in_1[3]), ._13__B4(in_2[3]), ._12__Y4(out_4[3]),
    ._11__A3(in_1[2]), ._10__B3(in_2[2]), ._9__Y3(out_4[2]));  // open: _8__GND, _16__Vcc
endmodule

module _8_bit_num_select (
  input  [7:0] in_1,
  input  [7:0] in_2,
  input  in_3,
  output [7:0] out_4
);

  _4_bit_num_select u_4_bit_num_select_1 (.in_1(in_1[3:0]), .in_2(in_2[3:0]), .in_3(in_3), .out_4(out_4[3:0]));
  _4_bit_num_select u_4_bit_num_select_2 (.in_1(in_1[7:4]), .in_2(in_2[7:4]), .in_3(in_3), .out_4(out_4[7:4]));
endmodule

module _16_bit_num_select (
  input  [15:0] in_1,
  input  [15:0] in_2,
  input  in_3,
  output [15:0] out_4
);

  _8_bit_num_select u_8_bit_num_select_1 (.in_1(in_1[7:0]), .in_2(in_2[7:0]), .out_4(out_4[7:0]), .in_3(in_3));
  _8_bit_num_select u_8_bit_num_select_2 (.in_1(in_1[15:8]), .in_2(in_2[15:8]), .out_4(out_4[15:8]), .in_3(in_3));
endmodule

module _32_bit_num_select (
  input  [31:0] in_1,
  input  [31:0] in_2,
  input  in_3,
  output [31:0] out_4
);

  _16_bit_num_select u_16_bit_num_select_1 (.in_1(in_1[15:0]), .in_2(in_2[15:0]), .out_4(out_4[15:0]), .in_3(in_3));
  _16_bit_num_select u_16_bit_num_select_2 (.in_1(in_1[31:16]), .in_2(in_2[31:16]), .out_4(out_4[31:16]), .in_3(in_3));
endmodule

module _1_bit_RS_with_ENB (
  input  [31:0] in_1,
  input  in_2,
  output [31:0] out_3
);

  wire [31:0] n1_bit_right_shifter_1_out_2;

  _1_bit_right_shifter u_1_bit_right_shifter_1 (.in_1(in_1), .out_2(n1_bit_right_shifter_1_out_2));
  _32_bit_num_select u_32_bit_num_select_1 (
    .in_1(n1_bit_right_shifter_1_out_2), .in_2(in_1), .out_4(out_3), .in_3(in_2));
endmodule

module _2_bit_RS_with_ENB (
  input  [31:0] in_1,
  input  in_2,
  output [31:0] out_3
);

  wire [31:0] n2_bit_right_shifter_1_out_2;

  _2_bit_right_shifter u_2_bit_right_shifter_1 (.in_1(in_1), .out_2(n2_bit_right_shifter_1_out_2));
  _32_bit_num_select u_32_bit_num_select_1 (
    .in_1(n2_bit_right_shifter_1_out_2), .in_2(in_1), .out_4(out_3), .in_3(in_2));
endmodule

module _4_bit_RS_with_ENB (
  input  [31:0] in_1,
  input  in_2,
  output [31:0] out_3
);

  wire [31:0] n4_bit_right_shifter_1_out_2;

  _4_bit_right_shifter u_4_bit_right_shifter_1 (.in_1(in_1), .out_2(n4_bit_right_shifter_1_out_2));
  _32_bit_num_select u_32_bit_num_select_1 (
    .in_1(n4_bit_right_shifter_1_out_2), .in_2(in_1), .out_4(out_3), .in_3(in_2));
endmodule

module _8_bit_RS_with_ENB (
  input  [31:0] in_1,
  input  in_2,
  output [31:0] out_3
);

  wire [31:0] n8_bit_right_shifter_1_out_2;

  _8_bit_right_shifter u_8_bit_right_shifter_1 (.in_1(in_1), .out_2(n8_bit_right_shifter_1_out_2));
  _32_bit_num_select u_32_bit_num_select_1 (
    .in_1(n8_bit_right_shifter_1_out_2), .in_2(in_1), .out_4(out_3), .in_3(in_2));
endmodule

module _16_bit_RS_with_ENB (
  input  [31:0] in_1,
  input  in_2,
  output [31:0] out_3
);

  wire [31:0] n16_bit_right_shifter_1_out_2;

  _16_bit_right_shifter u_16_bit_right_shifter_1 (.in_1(in_1), .out_2(n16_bit_right_shifter_1_out_2));
  _32_bit_num_select u_32_bit_num_select_1 (
    .in_1(n16_bit_right_shifter_1_out_2), .in_2(in_1), .out_4(out_3), .in_3(in_2));
endmodule

module _1_bit_LS_with_ENB (
  input  [31:0] in_1,
  input  in_2,
  output [31:0] out_3
);

  wire [31:0] n1_bit_left_shifter_1_out_2;

  _1_bit_left_shifter u_1_bit_left_shifter_1 (.in_1(in_1), .out_2(n1_bit_left_shifter_1_out_2));
  _32_bit_num_select u_32_bit_num_select_1 (
    .in_1(n1_bit_left_shifter_1_out_2), .in_2(in_1), .out_4(out_3), .in_3(in_2));
endmodule

module _2_bit_LS_with_ENB (
  input  [31:0] in_1,
  input  in_2,
  output [31:0] out_3
);

  wire [31:0] n2_bit_left_shifter_1_out_2;

  _2_bit_left_shifter u_2_bit_left_shifter_1 (.in_1(in_1), .out_2(n2_bit_left_shifter_1_out_2));
  _32_bit_num_select u_32_bit_num_select_1 (
    .in_1(n2_bit_left_shifter_1_out_2), .in_2(in_1), .out_4(out_3), .in_3(in_2));
endmodule

module _4_bit_LS_with_ENB (
  input  [31:0] in_1,
  input  in_2,
  output [31:0] out_3
);

  wire [31:0] n4_bit_left_shifter_1_out_2;

  _4_bit_left_shifter u_4_bit_left_shifter_1 (.in_1(in_1), .out_2(n4_bit_left_shifter_1_out_2));
  _32_bit_num_select u_32_bit_num_select_1 (
    .in_1(n4_bit_left_shifter_1_out_2), .in_2(in_1), .out_4(out_3), .in_3(in_2));
endmodule

module _8_bit_LS_with_ENB (
  input  [31:0] in_1,
  input  in_2,
  output [31:0] out_3
);

  wire [31:0] n8_bit_left_shifter_1_out_2;

  _8_bit_left_shifter u_8_bit_left_shifter_1 (.in_1(in_1), .out_2(n8_bit_left_shifter_1_out_2));
  _32_bit_num_select u_32_bit_num_select_1 (
    .in_1(n8_bit_left_shifter_1_out_2), .in_2(in_1), .out_4(out_3), .in_3(in_2));
endmodule

module _16_bit_LS_with_ENB (
  input  [31:0] in_1,
  input  in_2,
  output [31:0] out_3
);

  wire [31:0] n16_bit_left_shifter_1_out_2;

  _16_bit_left_shifter u_16_bit_left_shifter_1 (.in_1(in_1), .out_2(n16_bit_left_shifter_1_out_2));
  _32_bit_num_select u_32_bit_num_select_1 (
    .in_1(n16_bit_left_shifter_1_out_2), .in_2(in_1), .out_4(out_3), .in_3(in_2));
endmodule
